# Fritzing sketch lab01 (saved by Fritzing 0.9.3b)
breadboards: 1

parts:
  Part1 = LinkIt ONE board
  R1 = Resistor [tolerance=±5% resistance=220 package=THT]
  LED1 = LED - 5mm [color="Red (633nm)" package="5 mm [THT]"]

nets:
  N1: Part1.pin_9, LED1.anode
  N2: Part1.pin_26, R1.Pin_0
  N3: R1.Pin_1, LED1.cathode
