# Fritzing sketch lab02 (saved by Fritzing 0.9.3b)
breadboards: 1

parts:
  Part1 = LinkIt ONE board
  R1 = Resistor [tolerance=±5% resistance=220 package=THT]
  LED1 = LED - 5mm [color="Red (633nm)" package="5 mm [THT]"]
  R2 = Rotary Potentiometer (Large) [maximum_resistance=100kΩ package=THT]

nets:
  N1: Part1.pin_9, LED1.anode
  N2: Part1.pin_23, R2.wiper
  N3: Part1.pin_26, R1.Pin_0
  N4: Part1.pin_27, Part1.pin_44, R2.leg1, R2.leg2
  N5: R1.Pin_1, LED1.cathode
