# Fritzing sketch lab03 (saved by Fritzing 0.9.3b)
breadboards: 1

parts:
  Part1 = LinkIt ONE board
  R1 = Resistor [tolerance=±5% resistance=1k package=THT]
  LED1 = LED - 5mm [color="Red (633nm)" package="5 mm [THT]"]
  button = Pushbutton [package="[THT]"]
  R2 = Resistor [tolerance=±5% resistance=1k package=THT]

nets:
  N1: Part1.pin_7, button.Pin_1, button.Pin_2, R2.Pin_0
  N2: Part1.pin_9, LED1.anode
  N3: Part1.pin_26, Part1.pin_35, R1.Pin_0, R2.Pin_1
  5V: Part1.pin_27, Part1.pin_44, button.Pin_3, button.Pin_4
  N4: R1.Pin_1, LED1.cathode
